# Fritzing sketch Generation1 (saved by Fritzing 0.9.3b)
circuit board: 8.46667cm x 5.64444cm
breadboards: 1

parts:
  Part1 = Arduino Uno (Rev3) - ICSP
  MAX471_Current_and_Voltage_Sensor1 = MAX471 Current and Voltage Sensor Module
  DHT1 = DHT11 Humitidy and Temperature Sensor (3 pins)
  D1 = SOLAR-IXYS [package=solarbit-12x1]
  X1 = USB Connectors [package=usb-a-s-nosilk]
  USBTTL1 = USB TTL Serial Cable
  Part2 = Logic Level Converter
  U1 = ESP8266 WiFi Module [part_number=ESP8266]
  Part3 = Soil Moisture Sensor
  R1 = Resistor [tolerance=±5% resistance=220 package="0603 [SMD]"]
  DS1 = DS18B20 1-Wire Temperature Sensor Probe Cable
  Reg1 = DC-DC CONVERTER [part_number=80633 package=dc-dc_converter]

nets:
  N1: Part1.A0, Part3.SIG
  N2: Part1.A1, MAX471_Current_and_Voltage_Sensor1.VT
  N3: Part1.A2, MAX471_Current_and_Voltage_Sensor1.AT
  N4: Part1.ICSP_MISO, Part1.5V, Part1.D12/MISO, DS1.DQ
  N5: Part1.D9_PWM, DHT1.DATA
  N6: Part1.D10_PWM/SS, Part2.RX2_HV
  N7: Part1.D11_PWM/MOSI, Part2.TX_HV
  N8: Part1.GND, MAX471_Current_and_Voltage_Sensor1.GND#8
  N9: Part1.VIN, MAX471_Current_and_Voltage_Sensor1.VOUT
  N10: MAX471_Current_and_Voltage_Sensor1.GND#10, USBTTL1.GND
  VIN: MAX471_Current_and_Voltage_Sensor1.VIN, USBTTL1.5V
  GND: MAX471_Current_and_Voltage_Sensor1.GND#12, MAX471_Current_and_Voltage_Sensor1.GND#13, DHT1.GND, Part2.GND, U1.GND, Part3.GND, DS1.GND, Reg1.IN-
  VDD: DHT1.VDD, Part2.HV, Part3.VCC, DS1.VDD, Reg1.IN+
  N11: D1.A, X1.GND
  N12: D1.C, X1.VBUS
  N13: Part2.RX2_LV, U1.RXD
  N14: Part2.LV, U1.VCC, R1.Pin_1, Reg1.OUT-, Reg1.OUT+
  N15: Part2.TX_LV, U1.TXD
  N16: U1.REST, R1.Pin_0

custom parts:
  MAX471 Current and Voltage Sensor Module: The MAX471 current and voltage sensor module is a bidirectional, highside current-sense amplifier. The current measurement maximum is 3 amps and the voltage measurement range is 3 to 25 volts. The operating voltage range is 3 to 36 volts.
  DHT11 Humitidy and Temperature Sensor (3 pins): DHT11 Humidity and Temperature Sensor (3 pins) from the design created by John De Cristofaro for Adafruit Industries.
  DC-DC CONVERTER: WYHP 5A constant current/voltage manufactured by Shenzhen Weiyapuhua Technology Co., Ltd
